# Fritzing sketch breadboard (saved by Fritzing 0.9.9b)

parts:
  U1 = ESP32-38PinWide [part_number=ESP32-38PinWide]
  Bauteil1 = Adafruit MAX98357A I2S 3W Class D Amplifier [part_number="Adafruit #3006"]
  Bauteil2 = Adafruit MAX98357A I2S 3W Class D Amplifier [part_number="Adafruit #3006"]
  Bauteil3 = Adafruit MAX98357A I2S 3W Class D Amplifier [part_number="Adafruit #3006"]
  Bauteil4 = Adafruit MAX98357A I2S 3W Class D Amplifier [part_number="Adafruit #3006"]
  Bauteil5 = Adafruit MAX98357A I2S 3W Class D Amplifier [part_number="Adafruit #3006"]  # not connected
  Bauteil6 = Adafruit MAX98357A I2S 3W Class D Amplifier [part_number="Adafruit #3006"]  # not connected
  R1 = Resistor [tolerance=±5% resistance=220 package="2512 [SMD]"]
  R2 = Resistor [tolerance=±5% resistance=220 package="2512 [SMD]"]

nets:
  N1: U1.GPIO35, Bauteil4.DIN
  N2: U1.GPIO32, Bauteil3.DIN
  N3: U1.GPIO33, Bauteil1.DIN
  N4: U1.GPIO25, Bauteil1.BCLK
  N5: U1.GPIO26, Bauteil1.LRCLK
  GND: U1.GND, Bauteil1.GND
  VIN: U1.VIN, Bauteil1.VIN
  N6: Bauteil1.SD_MODE, R1.Pin_0
  N7: Bauteil2.SD_MODE, R2.Pin_0

notes:
  Coil 1
  Coil 2
  Coil 3
  Coil 4
  Coil 5
  Coil 6
  power in (5V)
  GND

custom parts:
  ESP32-38PinWide: Generic 38-Pin ESP32 with wide format (only access to one side of pins on a breadboard) based on Stephen Lilley's HiLetgo ESP-WROOM-32 ESP32 ESP-32S Development Board.
  Adafruit MAX98357A I2S 3W Class D Amplifier: Listen to this good news - we now have an all in one digital audio amp breakout board that works incredibly well with the Raspberry Pi! If you're looking for an easy and low cost way to get you digital sound files bumpin' then the MAX08357 I2S Amp Breakout is for you. It takes standard I2S digital audio input and, not only decodes it into analog, but also amplifies it directly into a speaker.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
